// Logisim project comprobación_IP.circ as structural Verilog: 5 circuits, main circuit main
// Bits de fragmentación y offset
module main (
  input  [7:0] in_1,
  input  [3:0] \Versión_IP ,
  input  [15:0] Bits_de_datos,
  input  [3:0] Lonx__Cab,
  input  [7:0] in_5,
  input  [7:0] TOS,
  input  [7:0] in_7,
  input  [15:0] Lonx__Data,
  input  [7:0] in_9,
  input  [15:0] Identificador,
  input  [7:0] in_11,
  input  [7:0] in_12,
  input  [7:0] in_13,
  input  [7:0] in_14,
  input  [7:0] TTL,
  input  [7:0] in_16,
  input  [7:0] Protocolo,
  input  [7:0] in_18,
  input  [15:0] Checksum,
  input  [7:0] in_20,
  input  [7:0] in_21,
  output OK,
  output \Cabecera_non_válida ,
  output \Tamaño_de_datos_non_válido ,
  output \Tipo_de_servicio_non_recoñecido ,
  output \Lonxitude_da_cabecera_non_válida ,
  output \Versión_IP_non_reconocida ,
  output \Fragmentación_non_válida ,
  output \Identificador_de_datagrama_non_válido ,
  output \Checksum_non_válido ,
  output \Protocolo_non_recoñecido ,
  output TTL_agotado,
  output \O_datagrama_non_é_para_este_equipo 
);

  wire CLK, comparator_1_eq, n1era_palabra_1_ok, n2a_palabra_1_ok, n3era_palabra_1_ok, not_1_out;
  wire [31:0] _0_31, _32_63, _64_95, _96_127, _128_159, MI_IP;

  // Probe on \Versión_IP 
  // Probe on Lonx__Cab
  // Probe on TOS
  // Probe on Lonx__Data
  // Probe on Identificador
  // Probe on TTL
  // Probe on Protocolo
  // Probe on Checksum
  Register #(.width(32)) register_1 (
    .D({\Versión_IP , Lonx__Cab, TOS, Lonx__Data}), .Q(_0_31), .clk(CLK));  // open: en, clr
  Register #(.width(32)) register_2 (.D({Identificador, {16{1'b0}}}), .Q(_32_63), .clk(CLK));  // open: en, clr
  Register #(.width(32)) register_3 (.D({TTL, Protocolo, Checksum}), .Q(_64_95), .clk(CLK));  // open: en, clr
  // Probe on in_9
  // Probe on in_14
  // Probe on in_1
  // Probe on in_5
  // Probe on in_7
  // Probe on in_11
  // Probe on in_12
  // Probe on in_13
  // Probe on in_16
  // Probe on in_18
  // Probe on in_20
  // Probe on in_21
  Clock clock_1 (.out(CLK));
  Register #(.width(32)) register_4 (.D({in_1, in_5, in_7, in_9}), .Q(_96_127), .clk(CLK));  // open: en, clr
  Register #(.width(32)) register_5 (.D({in_11, in_12, in_13, in_14}), .Q(_128_159), .clk(CLK));  // open: en, clr
  Register #(.width(32)) register_6 (.D({in_16, in_18, in_20, in_21}), .Q(MI_IP), .clk(CLK));  // open: en, clr
  not not_1 (not_1_out, CLK);
  _2a_palabra u_2a_palabra_1 (
    .Segunda_palabra(_32_63), .CLK(not_1_out), .OK(n2a_palabra_1_ok),
    .Invalid_Frag(\Fragmentación_non_válida ), .Invalid_ID(\Identificador_de_datagrama_non_válido ));
  _3era_palabra u_3era_palabra_1 (
    .Terceira_palabra(_64_95), .Quinta_palabra(_0_31), .Cuarta_palabra(_32_63), .Segunda_palabra(_96_127),
    .Primeira_palabra(_128_159), .OK(n3era_palabra_1_ok), .Invalid_checksum(\Checksum_non_válido ),
    .Invalid_protocol(\Protocolo_non_recoñecido ), .Invalid_TTL(TTL_agotado));
  Comparator #(.width(32), .mode("unsigned")) comparator_1 (
    .a(MI_IP), .b(_128_159), .eq(comparator_1_eq));  // open: gt, lt
  _1era_palabra u_1era_palabra_1 (
    .Bits_de_datos(Bits_de_datos), .Primeira_palabra(_0_31), .OK(n1era_palabra_1_ok),
    .Invalid_Data_Length(\Tamaño_de_datos_non_válido ), .Invalid_TOS(\Tipo_de_servicio_non_recoñecido ),
    .Invalid_Header_Length(\Lonxitude_da_cabecera_non_válida ),
    .Invalid_IP_Version(\Versión_IP_non_reconocida ));
  and and_1 (OK, comparator_1_eq, n3era_palabra_1_ok, n2a_palabra_1_ok, n1era_palabra_1_ok);
  not not_2 (\O_datagrama_non_é_para_este_equipo , comparator_1_eq);
  not not_3 (\Cabecera_non_válida , OK);

  // Notes on the sheet:
  //   Bits de fragmentación
  //   e offset
  //   Traballo persoal: Comprobación de cabeceiras HTTP por Héctor Padín Torrente
  //   e según os campos recibidos indicará se é válida ou non, e no caso de que non o fose, diríanos 
  //   que campo(s) recibiu de maneira incorrecta.Está implementado para recoñecer solo o protocolo
  //   TCP/IP, polo tanto se non usa o protocolo TCP (0x06) o circuíto dirá que é invalido.
  //   O exercicio sobre o diseño dun circuíto lóxico capaz de validar os campos dunha cabeceira HTTP
  //   (excepto TOS e fragmentación que tendrán todos os bits a 0). O circuíto recibe unha cabeceira descomposta
  //   IP destino
  //   IP do noso dispositivo
  //   (non é parte da cabeceira)
  //   IP de orixe
  //   IP de destino
endmodule

module _1era_palabra (
  input  [15:0] Bits_de_datos,
  input  [31:0] Primeira_palabra,
  output OK,
  output Invalid_Data_Length,
  output Invalid_TOS,
  output Invalid_Header_Length,
  output Invalid_IP_Version
);

  wire comparator_1_eq, comparator_2_eq, comparator_3_eq, comparator_4_eq;

  // Probe on Bits_de_datos
  // Probe on Primeira_palabra[15:0]
  Comparator #(.width(16), .mode("unsigned")) comparator_1 (
    .a(Bits_de_datos), .b(Primeira_palabra[15:0]), .eq(comparator_1_eq));  // open: gt, lt
  Comparator #(.mode("unsigned")) comparator_2 (
    .a(Primeira_palabra[23:16]), .b({8{1'b0}}), .eq(comparator_2_eq));  // open: gt, lt
  Comparator #(.width(4), .mode("unsigned")) comparator_3 (
    .a(Primeira_palabra[27:24]), .b(4'b0101), .eq(comparator_3_eq));  // open: gt, lt
  Comparator #(.width(4), .mode("unsigned")) comparator_4 (
    .a(Primeira_palabra[31:28]), .b(4'b0100), .eq(comparator_4_eq));  // open: gt, lt
  not not_1 (Invalid_Data_Length, comparator_1_eq);
  not not_2 (Invalid_IP_Version, comparator_4_eq);
  not not_3 (Invalid_TOS, comparator_2_eq);
  not not_4 (Invalid_Header_Length, comparator_3_eq);
  and and_1 (OK, comparator_1_eq, comparator_2_eq, comparator_3_eq, comparator_4_eq);

  // Notes on the sheet:
  //   sen incluír a cabeceira
  //   Lonxitude da cabeceira
  //   Versión IP
  //   Lonxitude total do datagrama recibido
  //   Tipe Of Service (non implementado)
  //   Polo tanto todos los bits estarán a 0
endmodule

module _2a_palabra (
  input  [31:0] Segunda_palabra,
  input  CLK,
  output OK,
  output Invalid_Frag,
  output Invalid_ID
);

  wire and_1_out, comparator_1_eq, comparator_2_eq, not_1_out;
  wire [15:0] register_1_q;

  Comparator #(.width(16), .mode("unsigned")) comparator_1 (
    .a(Segunda_palabra[15:0]), .b({16{1'b0}}), .eq(comparator_1_eq));  // open: gt, lt
  Comparator #(.width(16), .mode("unsigned")) comparator_2 (
    .a(Segunda_palabra[31:16]), .b(register_1_q), .eq(comparator_2_eq));  // open: gt, lt
  Register #(.width(16)) register_1 (.D(Segunda_palabra[31:16]), .Q(register_1_q), .clk(and_1_out));  // open: en, clr
  not not_1 (not_1_out, comparator_2_eq);
  and and_1 (and_1_out, not_1_out, CLK);
  not not_2 (Invalid_Frag, comparator_1_eq);
  and and_2 (OK, comparator_1_eq, not_1_out);
  not not_3 (Invalid_ID, not_1_out);

  // Notes on the sheet:
  //   Bits para a fragmentación
  //   (non implementado)
  //   Identificación
  //   Último id recibido
endmodule

module _3era_palabra (
  input  [31:0] Quinta_palabra,
  input  [31:0] Cuarta_palabra,
  input  [31:0] Segunda_palabra,
  input  [31:0] Primeira_palabra,
  input  [31:0] Terceira_palabra,
  output OK,
  output Invalid_checksum,
  output Invalid_protocol,
  output Invalid_TTL
);

  wire comparator_1_lt, comparator_2_eq, comparator_3_eq;
  wire [15:0] sumc1_1_salida;

  Comparator #(.mode("unsigned")) comparator_1 (
    .a({8{1'b0}}), .b(Terceira_palabra[31:24]), .lt(comparator_1_lt));  // open: gt, eq
  SumC1 sumc1_1 (
    .Primeira_palabra(Primeira_palabra), .Segunda_palabra(Segunda_palabra),
    .Terceira_palabra(Terceira_palabra), .Cuarta_palabra(Cuarta_palabra), .Quinta_palabra(Quinta_palabra),
    .Salida(sumc1_1_salida));
  Comparator #(.width(16), .mode("unsigned")) comparator_2 (
    .a(sumc1_1_salida), .b(Terceira_palabra[15:0]), .eq(comparator_2_eq));  // open: gt, lt
  Comparator #(.mode("unsigned")) comparator_3 (
    .a(8'h6), .b(Terceira_palabra[23:16]), .eq(comparator_3_eq));  // open: gt, lt
  not not_1 (Invalid_checksum, comparator_2_eq);
  and and_1 (OK, comparator_2_eq, comparator_3_eq, comparator_1_lt);
  not not_2 (Invalid_protocol, comparator_3_eq);
  not not_3 (Invalid_TTL, comparator_1_lt);

  // Notes on the sheet:
  //   TTL
  //   Checksum
  //   Protocolo
  //   Sólo se implementou para o
  //   protocolo TCP (0x06)
endmodule

module SumC1 (
  input  [31:0] Primeira_palabra,
  input  [31:0] Segunda_palabra,
  input  [31:0] Terceira_palabra,
  input  [31:0] Cuarta_palabra,
  input  [31:0] Quinta_palabra,
  output [15:0] Salida
);

  wire [15:0] adder_1_out, adder_2_out, adder_3_out, adder_4_out, adder_5_out, adder_6_out, adder_7_out,
       adder_8_out, adder_9_out;

  Adder #(.width(16)) adder_1 (
    .a(Primeira_palabra[15:0]), .b(Primeira_palabra[31:16]), .out(adder_1_out));  // open: cin, cout
  Adder #(.width(16)) adder_2 (.a(adder_1_out), .b(Segunda_palabra[31:16]), .out(adder_2_out));  // open: cin, cout
  Adder #(.width(16)) adder_3 (.a(adder_2_out), .b(Segunda_palabra[15:0]), .out(adder_3_out));  // open: cin, cout
  Adder #(.width(16)) adder_4 (.a(adder_3_out), .b(Terceira_palabra[31:16]), .out(adder_4_out));  // open: cin, cout
  Adder #(.width(16)) adder_5 (.a(adder_4_out), .b({16{1'b0}}), .out(adder_5_out));  // open: cin, cout
  Adder #(.width(16)) adder_6 (.a(adder_5_out), .b(Cuarta_palabra[31:16]), .out(adder_6_out));  // open: cin, cout
  Adder #(.width(16)) adder_7 (.a(adder_6_out), .b(Cuarta_palabra[15:0]), .out(adder_7_out));  // open: cin, cout
  Adder #(.width(16)) adder_8 (.a(adder_7_out), .b(Quinta_palabra[31:16]), .out(adder_8_out));  // open: cin, cout
  Adder #(.width(16)) adder_9 (.a(adder_8_out), .b(Quinta_palabra[15:0]), .out(adder_9_out));  // open: cin, cout
  assign Salida = ~adder_9_out;  // NOT_Gate not_1, 16 bits wide

  // Notes on the sheet:
  //   Bits de Checksum
endmodule
